# Fritzing sketch ObstacleRobot (saved by Fritzing 0.9.2b)

parts:
  M1 = DC Motor
  M2 = DC Motor
  VCC2 = Battery
  VCC4 = Battery
  Part4 = SRF05 Ultrasonic Rangefinder
  S1 = H-Bridge with L298N
  Arduino_UNO = Arduino Uno (Rev3)
  VCC3 = Battery
  J1 = Basic Servo

nets:
  N1: M1.pin_1, S1.M1-01
  N2: M1.pin_2, S1.M1-02
  N3: M2.pin_1, S1.M2-02
  N4: M2.pin_2, S1.M2-01
  N5: VCC2.-, VCC3.+
  N6: VCC2.+, S1.12V
  GND: VCC4.-, Part4.GND, Arduino_UNO.GND, J1.gnd
  N7: VCC4.+, VCC3.-
  VCC: Part4.VCC, Arduino_UNO.5V, J1.vcc
  N8: Part4.Trig, Arduino_UNO.D12/MISO
  N9: Part4.Echo, Arduino_UNO.D13/SCK
  5V: S1.5V, Arduino_UNO.VIN
  N10: S1.ENA, Arduino_UNO.D11_PWM/MOSI
  N11: S1.IN1, Arduino_UNO.D9_PWM
  N12: S1.IN2, Arduino_UNO.D8
  N13: S1.IN3, Arduino_UNO.D7
  N14: S1.IN4, Arduino_UNO.D6_PWM
  N15: S1.ENB, Arduino_UNO.D5_PWM
  N16: Arduino_UNO.D2, J1.pulse

custom parts:
  H-Bridge with L298N: h-bridge
